# Fritzing sketch controller (saved by Fritzing 0.9.2b)

parts:
  Pro_Micro1 = Pro Micro
  S1 = Pushbutton [package="[THT]"]
  S2 = Pushbutton [package="[THT]"]
  S3 = Pushbutton [package="[THT]"]
  S4 = Pushbutton [package="[THT]"]
  S5 = Pushbutton [package="[THT]"]
  S6 = Pushbutton [package="[THT]"]
  S7 = Pushbutton [package="[THT]"]
  RE1 = Rotary Encoder [package=THT]
  RE2 = Rotary Encoder [package=THT]
  LED2 = Super Flux LED blue [color=Blue]
  LED3 = Super Flux LED blue [color=Blue]
  LED4 = Super Flux LED blue [color=Blue]
  LED5 = Super Flux LED blue [color=Blue]
  LED6 = Super Flux LED blue [color=Blue]
  LED7 = Super Flux LED blue [color=Blue]
  LED8 = Super Flux LED blue [color=Blue]
  R1 = Resistor [tolerance=±5% resistance=220 package="2512 [SMD]"]
  R2 = Resistor [tolerance=±5% resistance=220 package="0603 [SMD]"]
  R3 = Resistor [tolerance=±5% resistance=220 package="2010 [SMD]"]
  R4 = Resistor [tolerance=±5% resistance=220 package="2010 [SMD]"]
  R5 = Resistor [tolerance=±5% resistance=220 package="2010 [SMD]"]
  R6 = Resistor [tolerance=±5% resistance=220 package="1206 [SMD]"]
  R7 = Resistor [tolerance=±5% resistance=220 package="1206 [SMD]"]
  R8 = Resistor [tolerance=±5% resistance=220 package="2010 [SMD]"]

nets:
  N1: Pro_Micro1.TX1, RE2.EncoderPinB
  N2: Pro_Micro1.RX0, RE2.EncoderPinA
  N3: Pro_Micro1.GND#3, RE2.EncoderPinC
  N4: Pro_Micro1.GND#4, S1.Pin_1, S1.Pin_2, S5.Pin_1, S5.Pin_2, S6.Pin_3, S6.Pin_4, LED5.cathode, LED6.anode, LED7.cathode
  N5: Pro_Micro1.D2, RE1.EncoderPinA
  N6: Pro_Micro1.D3, RE1.EncoderPinB
  N7: Pro_Micro1.D4, R5.Pin_1
  N8: Pro_Micro1.D5, R4.Pin_1
  N9: Pro_Micro1.D6, S1.Pin_4
  N10: Pro_Micro1.D7, S2.Pin_3, S2.Pin_4
  N11: Pro_Micro1.D8, R6.Pin_1
  N12: Pro_Micro1.D9, S5.Pin_3, S5.Pin_4
  N13: Pro_Micro1.D10, S6.Pin_2
  N14: Pro_Micro1.D16/MOSI, R7.Pin_0
  N15: Pro_Micro1.D14/MISO, S3.Pin_1, S3.Pin_2
  N16: Pro_Micro1.D15/SCLK, S4.Pin_1, S4.Pin_2
  N17: Pro_Micro1.D18/A0, R2.Pin_0
  N18: Pro_Micro1.D19/A1, R3.Pin_0
  N19: Pro_Micro1.D20/A2, S7.Pin_3, S7.Pin_4
  N20: Pro_Micro1.D21/A3, R1.Pin_1, R8.Pin_0
  N21: Pro_Micro1.GND#23, RE1.EncoderPinC
  N22: S2.Pin_1, S2.Pin_2, S7.Pin_1, S7.Pin_2, LED4.cathode, LED8.anode
  N23: S3.Pin_3, LED3.cathode
  N24: S4.Pin_3, S4.Pin_4, LED2.cathode
  N25: LED2.anode, R3.Pin_1
  N26: LED3.anode, R2.Pin_1
  N27: LED4.anode, R4.Pin_0
  N28: LED5.anode, R5.Pin_0
  N29: LED6.cathode, R7.Pin_1
  N30: LED7.anode, R6.Pin_0
  N31: LED8.cathode, R8.Pin_1

custom parts:
  Pro Micro: The SparkFun Pro Micro is a complete USB-based microcontoller development system, in a very small footprint, capable of implementing many types of projects. All programming can be done via the USB port.
